# Fritzing sketch Project (saved by Fritzing 0.9.3b)
breadboards: 1

parts:
  U1 = NodeMCU V1.0
  A1 = DHT22 module
  M1 = fc-51 [package=THT]
  Part1 = MQ-7 breakout

nets:
  N1: U1.D1, M1.pin1
  N2: U1.D3, A1.DAT
  N3: U1.3V3, M1.pin3
  GND: U1.GND, A1.GND, M1.pin2, Part1.GND
  VCC: U1.Vin, A1.VCC, Part1.VCC
  N4: U1.A0, Part1.AO

custom parts:
  NodeMCU V1.0: ESP8266 based NodeMCU
  DHT22 module: DHT22 module. Pins GND VCC Data.
  MQ-7 breakout: SKU: 101282
